# Fritzing sketch offline-PM-sensor (saved by Fritzing 0.9.3b)
breadboards: 1

parts:
  ZS-042_RTC1 = ZS-042 RTC Module
  Part1 = Adafruit HUZZAH32 ESP32 Feather [part_number="Adafruit #3405"]
  SDS011_(TX_RX_GND_X_5V) = Header 5x2 [package=2x5-raf]
  LED1 = LED - 5mm [color="Red (633nm)" package="5 mm [THT]"]
  S1 = Momentary Switch [package=ksa_sealed_tac_switch]
  R1 = Resistor [tolerance=±5% resistance=1k package=THT]
  R2 = Resistor [tolerance=±5% resistance=10k package=THT]
  Q1 = npn-Powertransistor [package="TO220 [THT]"]
  R3 = Resistor [tolerance=±5% resistance=10k package="0402 [SMD]"]

nets:
  GND: ZS-042_RTC1.GND, Part1.GND, LED1.cathode, R2.Pin_1, Q1.emitter
  N1: ZS-042_RTC1.VCC, Part1.VBUS, SDS011_(TX_RX_GND_X_5V).1
  N2: ZS-042_RTC1.SDA, Part1.SDA
  N3: ZS-042_RTC1.SCL, Part1.SCL
  N4: Part1.IO17, SDS011_(TX_RX_GND_X_5V).7
  N5: Part1.IO16, SDS011_(TX_RX_GND_X_5V).9
  N6: Part1.3.3V, S1.4
  N7: Part1.IO12_A11, R1.Pin_1
  N8: Part1.IO33_A9, S1.1
  N9: Part1.IO32_A7, R3.Pin_1
  N10: SDS011_(TX_RX_GND_X_5V).5, Q1.collector
  N11: LED1.anode, R1.Pin_0
  N12: S1.2, R2.Pin_0
  N13: Q1.base, R3.Pin_0

notes:
  Button to start wifi AP and web server.
  DS3231 Real time clock (with 3.3V battery backup)
  10K resistor to a TIP120 transistor
